// Logisim project automat.circ as structural Verilog: 1 circuit, main circuit main
module main (
  input  X,
  output S1,
  output S2,
  output S3,
  output Y
);

  wire and_1_out, and_2_out, and_3_out, and_4_out, and_5_out, and_6_out, and_7_out, and_8_out, clock_1_out,
       J1_K1_qn, J2_K2_qn, J3_K3_qn, not_1_out, not_2_out, not_3_out, not_4_out, not_5_out, not_6_out,
       or_1_out, or_2_out;

  not not_1 (not_1_out, S2);
  not not_2 (not_2_out, S1);
  not not_3 (not_3_out, S3);
  not not_4 (not_4_out, S2);
  not not_5 (not_5_out, S1);
  not not_6 (not_6_out, X);
  and and_1 (and_1_out, not_1_out, S3);
  and and_2 (and_2_out, S2, S3);
  and and_3 (and_3_out, not_2_out, S3);
  and and_4 (and_4_out, not_2_out, S2);
  and and_5 (and_5_out, not_2_out, not_3_out, X);
  and and_6 (and_6_out, not_4_out, S3);
  and and_7 (and_7_out, S3, not_5_out, not_6_out);
  and and_8 (and_8_out, not_3_out, S2);
  Clock clock_1 (.out(clock_1_out));
  or or_1 (or_1_out, and_4_out, and_5_out);
  or or_2 (or_2_out, and_6_out, and_7_out);
  or or_3 (Y, and_1_out, and_8_out);
  J_K_Flip_Flop J1_K1 (.J(and_2_out), .clk(clock_1_out), .K(S3), .Q(S1), .Qn(J1_K1_qn));  // open: preset, en, reset
  J_K_Flip_Flop J2_K2 (
    .J(and_3_out), .clk(clock_1_out), .K(and_3_out), .Q(S2), .Qn(J2_K2_qn));  // open: preset, en, reset
  J_K_Flip_Flop J3_K3 (
    .J(or_1_out), .clk(clock_1_out), .K(or_2_out), .Q(S3), .Qn(J3_K3_qn));  // open: preset, en, reset
endmodule
